# Fritzing sketch buzzereater (saved by Fritzing 0.9.3b)
circuit board: 7.85136cm x 5.35cm
breadboards: 1

parts:
  Q1 = NPN-Transistor [package="TO92 [THT]"]
  D1 = Rectifier Diode [part_number=1N4001 package="300 mil [THT]"]
  R4 = Resistor [tolerance=±5% resistance=220 package=THT]
  U1 = Vibration Motor- ROB-08449 [package=vibe-motor-10mm]
  Part5 = Adafruit FONA - Mini Cellular GSM Breakout
  J2 = female pin header, 12 pins [form="♀ (female)"]
  J3 = female pin header, 12 pins [form="♀ (female)"]
  J4 = female pin header, 2 pins [form="♀ (female)"]
  J1 = female pin header, 5 pins [form="♀ (female)"]

nets:
  N1: Q1.E, Part5.PWRKEY_5V, Part5.GND, J2.pin2, J4.pin2, J1.pin1
  N2: Q1.B, R4.Pin_1
  N3: Q1.C, D1.anode, U1.-
  N4: D1.cathode, U1.+, Part5.VCCIO, J2.pin4, J1.pin2
  N5: R4.Pin_0, J2.pin6
  N6: Part5.RXD_5V, J3.pin4
  N7: Part5.TXD_5V, J2.pin9
  N8: Part5.RESET_5V, J3.pin5
  N9: Part5.VBAT, J3.pin8
  N10: J2.pin1, J3.pin7
  N11: J2.pin5, J4.pin1
  N12: J3.pin1, J1.pin3
  N13: J3.pin11, J1.pin5
  N14: J3.pin12, J1.pin4

notes:
  OLED
  ARDUINO
  FONA
  MOTOR
  DIODE
  NPN
  220
  BUZZER V2
  Button
  DATA
  CLK
  RST
  5V
  GND

custom parts:
  Adafruit FONA - Mini Cellular GSM Breakout: An all-in-one cellular phone module that lets you add voice, text, SMS and GPRS data to your project. Quad-band 850/900/1800/1900MHz - connect onto any global GSM network with any 2G SIM. Includes an onboard LiPoly battery charging circuitry so you can take your project on the go. Also works as an FM radio receiver.
